// Logisim project registerfile.circ as structural Verilog: 1 circuit, main circuit main
module main (
  input  [1:0] ReadReg1,
  input  [7:0] RegDataW,
  input  RegWrite,
  input  [1:0] WriteReg,
  input  [1:0] ReadReg2,
  output [7:0] RegData1,
  output [7:0] RegData2
);

  wire c_signal1_out, c_signal2_out, c_signal_out, c_singal0_out, clock_r_out, decoder_1_out0,
       decoder_1_out1, decoder_1_out2, decoder_1_out3;
  wire [7:0] X0_q, X1_q, X2_q, X3_q;

  Clock clock_r (.out(clock_r_out));
  Decoder #(.select(2)) decoder_1 (
    .out0(decoder_1_out0), .out1(decoder_1_out1), .out2(decoder_1_out2), .out3(decoder_1_out3), .sel(WriteReg));  // open: en
  and c_singal0 (c_singal0_out, decoder_1_out0, RegWrite);
  and c_signal1 (c_signal1_out, decoder_1_out1, RegWrite);
  and c_signal2 (c_signal2_out, decoder_1_out2, RegWrite);
  and c_signal (c_signal_out, decoder_1_out3, RegWrite);
  Register X0 (.D(RegDataW), .en(c_singal0_out), .clk(clock_r_out), .Q(X0_q));  // open: clr
  Register X1 (.D(RegDataW), .en(c_signal1_out), .clk(clock_r_out), .Q(X1_q));  // open: clr
  Register X2 (.D(RegDataW), .en(c_signal2_out), .clk(clock_r_out), .Q(X2_q));  // open: clr
  Register X3 (.D(RegDataW), .en(c_signal_out), .clk(clock_r_out), .Q(X3_q));  // open: clr
  Multiplexer #(.select(2), .width(8)) multiplexer_1 (
    .in0(X0_q), .in1(X1_q), .in2(X2_q), .in3(X3_q), .out(RegData1), .sel(ReadReg1));
  Multiplexer #(.select(2), .width(8)) multiplexer_2 (
    .in0(X0_q), .in1(X1_q), .in2(X2_q), .in3(X3_q), .out(RegData2), .sel(ReadReg2));

  // Notes on the sheet:
  //   Decoder
  //   Alisha Patel - I pledge my honor that I have abided by the Stevens Honor System.
  //   Mulitplexer1
  //   Multiplexer2
endmodule
