// Logisim project microprocessor.circ as structural Verilog: 1 circuit, main circuit main
module main (
  output [7:0] out_1,
  output [7:0] RegData1,
  output [7:0] RegData2
);

  wire and_1_out, and_2_out, and_3_out, and_4_out, and_5_out, and_6_out, and_7_out, c_signal1_out,
       c_signal2_out, c_signal_out, c_singal0_out, cc_pc_out, clock_1_out, decoder_1_out0, decoder_1_out1,
       decoder_1_out2, decoder_1_out3, not_1_out, not_2_out, not_3_out, not_4_out, not_5_out, not_6_out,
       not_7_out, or_1_out, or_2_out, or_3_out, or_4_out, or_5_out;
  wire [1:0] multiplexer_3_out;
  wire [3:0] multiplexer_5_out, multiplexer_5_out_2;
  wire [7:0] adder_1_out, adder_2_out, bit_extender_1_out, instruc_mem_dout, multiplexer_4_out, or_6_out,
       PC_q, ram_1_dout, undriven, X1_q, X2_q, X3_q;

  Adder adder_1 (.a(PC_q), .b(8'h1), .out(adder_1_out));  // open: cin, cout
  Clock cc_pc (.out(cc_pc_out));
  Register PC (.D(adder_1_out), .en(1'b1), .clk(cc_pc_out), .Q(PC_q));  // open: clr
  RAM #(.enables("line")) instruc_mem (
    .addr(PC_q), .we(1'b0), .oe(1'b1), .clk(cc_pc_out), .dout(instruc_mem_dout));  // open: din
  Decoder #(.select(2)) decoder_1 (
    .out0(decoder_1_out0), .out1(decoder_1_out1), .out2(decoder_1_out2), .out3(decoder_1_out3),
    .sel(instruc_mem_dout[3:2]));  // open: en
  and and_1 (and_1_out, PC_q[0], PC_q[1], PC_q[2], PC_q[3], PC_q[5], PC_q[6], PC_q[7], PC_q[7]);
  and c_singal0 (c_singal0_out, decoder_1_out0, or_3_out);
  and c_signal1 (c_signal1_out, decoder_1_out1, or_3_out);
  and c_signal2 (c_signal2_out, decoder_1_out2, or_3_out);
  and c_signal (c_signal_out, decoder_1_out3, or_3_out);
  Register X0 (.D(out_1), .en(c_singal0_out), .clk(cc_pc_out), .clr(and_1_out));  // open: Q
  Register X1 (.D(out_1), .en(c_signal1_out), .clk(cc_pc_out), .Q(X1_q), .clr(and_1_out));
  Register X2 (.D(out_1), .en(c_signal2_out), .clk(cc_pc_out), .Q(X2_q), .clr(and_1_out));
  Register X3 (.D(out_1), .en(c_signal_out), .clk(cc_pc_out), .Q(X3_q), .clr(and_1_out));
  Multiplexer #(.select(2), .width(8)) multiplexer_1 (
    .in0(undriven), .in1(X1_q), .in2(X2_q), .in3(X3_q), .out(RegData1), .sel(instruc_mem_dout[5:4]));
  Multiplexer #(.select(2), .width(8)) multiplexer_2 (
    .in0(undriven), .in1(X1_q), .in2(X2_q), .in3(X3_q), .out(RegData2), .sel(multiplexer_3_out));
  not not_1 (not_1_out, instruc_mem_dout[0]);
  or or_1 (or_1_out, instruc_mem_dout[0], not_1_out);
  not not_2 (not_2_out, instruc_mem_dout[1]);
  or or_2 (or_2_out, not_2_out, instruc_mem_dout[1]);
  or or_3 (or_3_out, or_1_out, or_2_out);
  Multiplexer #(.width(2)) multiplexer_3 (
    .in0(instruc_mem_dout[3:2]), .in1(instruc_mem_dout[7:6]), .out(multiplexer_3_out), .sel(or_4_out));
  and and_2 (and_2_out, instruc_mem_dout[1], instruc_mem_dout[1]);
  Multiplexer #(.width(8)) multiplexer_4 (
    .in0(RegData2), .in1(bit_extender_1_out), .out(multiplexer_4_out), .sel(or_5_out));
  not not_3 (not_3_out, instruc_mem_dout[1]);
  not not_4 (not_4_out, instruc_mem_dout[0]);
  and and_3 (and_3_out, not_3_out, not_4_out);
  or or_4 (or_4_out, and_2_out, and_3_out);
  assign bit_extender_1_out = {{6{1'b0}}, instruc_mem_dout[7:6]};  // Bit_Extender bit_extender_1
  not not_5 (not_5_out, instruc_mem_dout[1]);
  and and_4 (and_4_out, instruc_mem_dout[0], not_5_out);
  not not_6 (not_6_out, instruc_mem_dout[0]);
  and and_5 (and_5_out, not_6_out, instruc_mem_dout[1]);
  or or_5 (or_5_out, and_4_out, and_5_out);
  Adder adder_2 (.a(RegData1), .b(multiplexer_4_out), .out(adder_2_out));  // open: cin, cout
  assign or_6_out = RegData1 | multiplexer_4_out;  // OR_Gate or_6, 8 bits wide
  and and_6 (and_6_out, instruc_mem_dout[1], instruc_mem_dout[0]);
  Hex_Digit_Display #(.decimalPoint("false")) LED (.value(multiplexer_5_out_2));
  Hex_Digit_Display #(.decimalPoint("false")) comp (.value(multiplexer_5_out));
  RAM ram_1 (
    .addr({multiplexer_5_out_2, multiplexer_5_out}), .we(1'b0), .oe(1'b1), .clk(clock_1_out),
    .dout(ram_1_dout));  // open: din
  Clock clock_1 (.out(clock_1_out));
  Multiplexer #(.width(8)) multiplexer_5 (
    .in0(adder_2_out), .in1(or_6_out), .out({multiplexer_5_out_2, multiplexer_5_out}), .sel(and_6_out));
  not not_7 (not_7_out, instruc_mem_dout[1]);
  and and_7 (and_7_out, not_7_out, instruc_mem_dout[0]);
  Multiplexer #(.width(8)) multiplexer_6 (
    .in0({multiplexer_5_out_2, multiplexer_5_out}), .in1(ram_1_dout), .out(out_1), .sel(and_7_out));

  // Notes on the sheet:
  //   CPU Name: DUFF
  //   Alisha Patel - I pledge my honor that I have abided by the Stevens Honor System.
  //   RegWrite
  //   Decoder
  //   WriteReg
  //   RegDataW
  //   opcode
  //   Mulitplexer1
  //   ReadReg1
  //   Multiplexer2
  //   ReadReg2
  //   RegWrite
  //   Reg2Loc
  //   imm
  //   ALUSrc
  //   ALUop
  //   MemtoReg
endmodule
